# Fritzing sketch jetson_finder_schmetics (saved by Fritzing 0.9.4)

parts:
  Jetson_Nano2 = Jetson Nano
  R4 = Resistor [tolerance=±5% resistance=2.2k package="1206 [SMD]"]
  R3 = Resistor [tolerance=±5% resistance=1k package="1206 [SMD]"]
  HC-SR04_Sensor_2 = HC-SR04 Ultrasonic Distance Sensor
  SW-1 = Vibration sensor module
  U3 = LM2596 step down module
  J1 = Power Jack [package=power_jack_smd]
  U4 = TRANSCHIPTC5747 [package=camera_sfv24r-2st_2]  # not connected

nets:
  N1: Jetson_Nano2.GPIO26, HC-SR04_Sensor_2.VCC
  N2: Jetson_Nano2.GND, Jetson_Nano2.GPIO12, HC-SR04_Sensor_2.TRIG, SW-1.Digital_output
  N3: Jetson_Nano2.ID_SC, R4.Pin_1, R3.Pin_1
  N4: R4.Pin_0, HC-SR04_Sensor_2.GND
  N5: R3.Pin_0, HC-SR04_Sensor_2.ECHO
  N6: U3.IN+, J1.GNDBREAK
  N7: U3.IN-, U3.OUT-, J1.GND

custom parts:
  Vibration sensor module: Single-roller type full induction trigger switch. When no vibration or tilt, the product is ON conduction state, and in the steady state, when a vibration or tilt, the switch will be rendered instantly disconnect the conductive resistance increases, generating a current pulse signal, thereby triggering circuit. The default state of the swith is close Digital output Supply voltage:3.3V-5V On-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
  LM2596 step down module: LM2596 DC-DC step down power supply module 3 A.
